// Logisim project Alu.circ as structural Verilog: 2 circuits, main circuit FULL ALU
module ALU (
  input  A,
  input  B,
  input  [2:0] in_3,
  input  Cin,
  input  Sub,
  input  Less,
  output Result,
  output Cout,
  output Set
);

  wire and_1_out, nor_1_out, or_1_out, xor_1_out, xor_2_out;

  xor xor_1 (xor_1_out, B, Sub);
  and and_1 (and_1_out, A, B);
  or or_1 (or_1_out, A, B);
  xor xor_2 (xor_2_out, A, B);
  nor nor_1 (nor_1_out, A, B);
  Adder #(.width(1)) adder_1 (.a(A), .b(xor_1_out), .out(Set), .cin(Cin), .cout(Cout));
  Multiplexer #(.select(3), .enable("false")) multiplexer_1 (
    .in0(and_1_out), .in1(or_1_out), .in2(xor_2_out), .in3(nor_1_out), .in4(Set), .in5(Less), .out(Result),
    .sel(in_3));  // open: in6, in7
endmodule

module FULL_ALU (
  input  [7:0] B,
  input  [7:0] A,
  input  [2:0] Operacao,
  input  \Subtração ,
  output [7:0] Saida
);

  wire alu_1_cout, alu_2_cout, alu_3_cout, alu_4_cout, alu_5_cout, alu_6_cout, alu_7_cout, alu_8_set;

  ALU alu_1 (
    .Sub(\Subtração ), .Less(alu_8_set), .Result(Saida[0]), .A(A[0]), .B(B[0]), .Cout(alu_1_cout),
    .in_3(Operacao));  // open: Cin, Set
  ALU alu_2 (
    .Cin(alu_1_cout), .Sub(\Subtração ), .Less(1'b0), .Result(Saida[1]), .A(A[1]), .B(B[1]),
    .Cout(alu_2_cout), .in_3(Operacao));  // open: Set
  ALU alu_3 (
    .Cin(alu_2_cout), .Sub(\Subtração ), .Less(1'b0), .Result(Saida[2]), .A(A[2]), .B(B[2]),
    .Cout(alu_3_cout), .in_3(Operacao));  // open: Set
  ALU alu_4 (
    .Cin(alu_3_cout), .Sub(\Subtração ), .Less(1'b0), .Result(Saida[3]), .A(A[3]), .B(B[3]),
    .Cout(alu_4_cout), .in_3(Operacao));  // open: Set
  ALU alu_5 (
    .Cin(alu_4_cout), .Sub(\Subtração ), .Less(1'b0), .Result(Saida[4]), .A(A[4]), .B(B[4]),
    .Cout(alu_5_cout), .in_3(Operacao));  // open: Set
  ALU alu_6 (
    .Cin(alu_5_cout), .Sub(\Subtração ), .Less(1'b0), .Result(Saida[5]), .A(A[5]), .B(B[5]),
    .Cout(alu_6_cout), .in_3(Operacao));  // open: Set
  ALU alu_7 (
    .Cin(alu_6_cout), .Sub(\Subtração ), .Less(1'b0), .Result(Saida[6]), .A(A[6]), .B(B[6]),
    .Cout(alu_7_cout), .in_3(Operacao));  // open: Set
  ALU alu_8 (
    .Cin(alu_7_cout), .Sub(\Subtração ), .Less(1'b0), .Result(Saida[7]), .A(A[7]), .B(B[7]), .Set(alu_8_set),
    .in_3(Operacao));  // open: Cout
endmodule
